// Logisim project SUMLATnuevo.circ as structural Verilog: 5 circuits, main circuit main
module main (
  input  [7:0] NumeroA,
  input  [7:0] NumeroB,
  input  c0,
  output c8,
  output [7:0] ResultadoDeLaSuma
);

  SUMLAT sumlat_1 (
    .a7(NumeroA[7]), .a6(NumeroA[6]), .a5(NumeroA[5]), .a4(NumeroA[4]), .a3(NumeroA[3]), .a2(NumeroA[2]),
    .a1(NumeroA[1]), .a0(NumeroA[0]), .b7(NumeroB[7]), .b6(NumeroB[6]), .b5(NumeroB[5]), .b4(NumeroB[4]),
    .b3(NumeroB[3]), .b2(NumeroB[2]), .b1(NumeroB[1]), .b0(NumeroB[0]), .c0(c0), .c8(c8),
    .s7(ResultadoDeLaSuma[7]), .s6(ResultadoDeLaSuma[6]), .s5(ResultadoDeLaSuma[5]),
    .s4(ResultadoDeLaSuma[4]), .s3(ResultadoDeLaSuma[3]), .s2(ResultadoDeLaSuma[2]),
    .s1(ResultadoDeLaSuma[1]), .s0(ResultadoDeLaSuma[0]));
endmodule

module BLOQUEB (
  input  PH,
  input  PL,
  input  GH,
  input  GL,
  input  Cin,
  output PHL,
  output GHL,
  output CH,
  output CL
);

  wire and_1_out, and_2_out;

  and and_1 (and_1_out, PH, GL);
  and and_2 (and_2_out, PL, Cin);
  and and_3 (PHL, PH, PL);
  or or_1 (GHL, GH, and_1_out);
  or or_2 (CH, and_2_out, GL);

  assign CL = Cin;
endmodule

module FAGP (
  input  ai,
  input  bi,
  input  ci,
  output pi,
  output gi,
  output si
);

  wire and_1_out, and_2_out, and_4_out, and_5_out, not_1_out, not_2_out, not_3_out, not_4_out, or_2_out;

  not not_1 (not_1_out, bi);
  not not_2 (not_2_out, ai);
  and and_1 (and_1_out, not_1_out, ai);
  and and_2 (and_2_out, bi, not_2_out);
  or or_1 (pi, ai, bi);
  and and_3 (gi, bi, ai);
  or or_2 (or_2_out, and_1_out, and_2_out);
  not not_3 (not_3_out, or_2_out);
  not not_4 (not_4_out, ci);
  and and_4 (and_4_out, not_3_out, ci);
  and and_5 (and_5_out, or_2_out, not_4_out);
  or or_3 (si, and_4_out, and_5_out);
endmodule

module SUMLAT (
  input  a7,
  input  a6,
  input  a5,
  input  a4,
  input  a3,
  input  a2,
  input  a1,
  input  a0,
  input  b7,
  input  b6,
  input  b5,
  input  b4,
  input  b3,
  input  b2,
  input  b1,
  input  b0,
  input  c0,
  output c8,
  output s7,
  output s6,
  output s5,
  output s4,
  output s3,
  output s2,
  output s1,
  output s0
);

  wire and_1_out, c0_N1, c0_N2, c0_N3, c1_N1, c2_N1, c2_N2, c3_N1, c4_N1, c4_N2, c4_N3, c5_N1, c6_N1, c6_N2,
       c7_N1, g0, g1, G1_0, g2, g3, G3_0, G3_2, g4, g5, G5_4, g6, g7, G7_0, G7_4, G7_6, p0, p1, P1_0, p2, p3,
       P3_0, P3_2, p4, p5, P5_4, p6, p7, P7_0, P7_4, P7_6;

  FAGP fagp_1 (.ai(a7), .bi(b7), .ci(c7_N1), .pi(p7), .gi(g7), .si(s7));
  BLOQUEB bloqueb_1 (.PH(p7), .PL(p6), .GH(g7), .GL(g6), .Cin(c6_N2), .PHL(P7_6), .GHL(G7_6), .CH(c7_N1), .CL(c6_N1));
  BLOQUEB bloqueb_2 (
    .PH(P7_6), .PL(P5_4), .GH(G7_6), .GL(G5_4), .Cin(c4_N3), .PHL(P7_4), .GHL(G7_4), .CH(c6_N2), .CL(c4_N2));
  BLOQUEB bloqueb_3 (
    .PH(P7_4), .PL(P3_0), .GH(G7_4), .GL(G3_0), .Cin(c0), .PHL(P7_0), .GHL(G7_0), .CH(c4_N3), .CL(c0_N3));
  and and_1 (and_1_out, c7_N1, p7);
  or or_1 (c8, and_1_out, g7);
  FAGP fagp_2 (.ai(a6), .bi(b6), .ci(c6_N1), .pi(p6), .gi(g6), .si(s6));
  FAGP fagp_3 (.ai(a5), .bi(b5), .ci(c5_N1), .pi(p5), .gi(g5), .si(s5));
  BLOQUEB bloqueb_4 (.PH(p5), .PL(p4), .GH(g5), .GL(g4), .Cin(c4_N2), .PHL(P5_4), .GHL(G5_4), .CH(c5_N1), .CL(c4_N1));
  FAGP fagp_4 (.ai(a4), .bi(b4), .ci(c4_N1), .pi(p4), .gi(g4), .si(s4));
  FAGP fagp_5 (.ai(a3), .bi(b3), .ci(c3_N1), .pi(p3), .gi(g3), .si(s3));
  BLOQUEB bloqueb_5 (.PH(p3), .PL(p2), .GH(g3), .GL(g2), .Cin(c2_N2), .PHL(P3_2), .GHL(G3_2), .CH(c3_N1), .CL(c2_N1));
  BLOQUEB bloqueb_6 (
    .PH(P3_2), .PL(P1_0), .GH(G3_2), .GL(G1_0), .Cin(c0_N3), .PHL(P3_0), .GHL(G3_0), .CH(c2_N2), .CL(c0_N2));
  FAGP fagp_6 (.ai(a2), .bi(b2), .ci(c2_N1), .pi(p2), .gi(g2), .si(s2));
  FAGP fagp_7 (.ai(a1), .bi(b1), .ci(c1_N1), .pi(p1), .gi(g1), .si(s1));
  BLOQUEB bloqueb_7 (.PH(p1), .PL(p0), .GH(g1), .GL(g0), .Cin(c0_N2), .PHL(P1_0), .GHL(G1_0), .CH(c1_N1), .CL(c0_N1));
  FAGP fagp_8 (.ai(a0), .bi(b0), .ci(c0_N1), .pi(p0), .gi(g0), .si(s0));
endmodule

module ModoNormal (
  input  Clear,
  output [7:0] out_2,
  output es52,
  output es55
);

  wire and_1_out, and_2_out, multiplexer_1_out, multiplexer_2_out, not_1_out, not_2_out, reloj_out,
       sumlat_1_c8;
  wire [7:0] multiplexer_3_out, multiplexer_4_out, multiplexer_5_out, or_1_out, or_2_out, sumlat_1_s0;

  Multiplexer #(.select(3)) multiplexer_1 (
    .in0(1'b1), .in1(1'b1), .in2(1'b1), .in3(1'b1), .in4(1'b0), .in5(1'b0), .in6(1'b0), .in7(1'b0),
    .out(multiplexer_1_out), .sel(out_2[2:0]));
  Multiplexer #(.select(3)) multiplexer_2 (
    .in0(1'b0), .in1(1'b0), .in2(1'b0), .in3(1'b0), .in4(1'b1), .in5(1'b0), .in6(1'b0), .in7(1'b1),
    .out(multiplexer_2_out), .sel(out_2[2:0]));
  Multiplexer #(.width(8)) multiplexer_3 (.in0({8{1'b0}}), .in1(8'h30), .out(multiplexer_3_out), .sel(Clear));
  Clock reloj (.out(reloj_out));
  Counter counter_1 (
    .load(multiplexer_2_out), .up(1'b1), .count(multiplexer_1_out), .clk(reloj_out), .D(or_1_out), .Q(out_2));  // open: clr, carry
  assign or_1_out = multiplexer_3_out | or_2_out;  // OR_Gate or_1, 8 bits wide
  not not_1 (not_1_out, out_2[1]);
  and and_1 (and_1_out, out_2[2], not_1_out);
  not not_2 (not_2_out, out_2[0]);
  and and_2 (and_2_out, out_2[0], out_2[1]);
  and and_3 (es52, and_1_out, not_2_out);
  and and_4 (es55, and_2_out, out_2[2]);
  SUMLAT sumlat_1 (
    .a7(1'b0), .a6(1'b0), .a5(1'b1), .a4(1'b1), .a3(1'b0), .a2(out_2[2]), .a1(out_2[1]), .a0(out_2[0]),
    .b7(1'b0), .b6(1'b0), .b5(1'b0), .b4(1'b0), .b3(1'b0), .b2(1'b0), .b1(1'b1), .b0(1'b1), .c0(1'b0),
    .c8(sumlat_1_c8), .s7(sumlat_1_s0[7]), .s6(sumlat_1_s0[6]), .s5(sumlat_1_s0[5]), .s4(sumlat_1_s0[4]),
    .s3(sumlat_1_s0[3]), .s2(sumlat_1_s0[2]), .s1(sumlat_1_s0[1]), .s0(sumlat_1_s0[0]));
  Multiplexer #(.width(8)) multiplexer_4 (.in0({8{1'b0}}), .in1(sumlat_1_s0), .out(multiplexer_4_out), .sel(es52));
  Multiplexer #(.width(8)) multiplexer_5 (.in0({8{1'b0}}), .in1(8'h30), .out(multiplexer_5_out), .sel(es55));
  assign or_2_out = multiplexer_4_out | multiplexer_5_out;  // OR_Gate or_2, 8 bits wide
  // also tied to GND on the sheet: sumlat_1_c8
endmodule
