// Logisim project santi.circ as structural Verilog: 3 circuits, main circuit main
module main (
  input  a7,
  input  a6,
  input  a5,
  input  a4,
  input  a3,
  input  a2,
  input  a1,
  input  a0,
  input  b7,
  input  b6,
  input  b5,
  input  b4,
  input  b3,
  input  b2,
  input  b1,
  input  b0,
  input  c0,
  output out_18,
  output out_19,
  output out_20,
  output out_21,
  output out_22,
  output out_23,
  output out_24,
  output out_25,
  output out_26
);

  wire c0_t, c1, c02, c2, c03, c3, c4, c5, c6, c7, c22, c42, c43, c62, g0, g1, G1_0, g2, g3, G3_0, G3_2, g4,
       g5, G5_4, g6, g7, G7_0, G7_4, G7_6, p0, p1, P1_0, p2, p3, P3_0, P3_2, p4, p5, P5_4, p6, P7_0, P7_4,
       P7_6;

  FAGP fagp_1 (.ai(a7), .bi(b7), .ci(c7), .si(out_19), .gi(g7), .pi(out_18));
  BLOQUEB bloqueb_1 (.PH(out_18), .PL(p6), .GH(g7), .GL(g6), .Cin(c62), .PHL(P7_6), .GHL(G7_6), .CH(c7), .CL(c6));
  BLOQUEB bloqueb_2 (.PH(P7_6), .PL(P5_4), .GH(G7_6), .GL(G5_4), .Cin(c43), .PHL(P7_4), .GHL(G7_4), .CH(c62), .CL(c42));
  BLOQUEB bloqueb_3 (.PH(P7_4), .PL(P3_0), .GH(G7_4), .GL(G3_0), .Cin(c0), .PHL(P7_0), .GHL(G7_0), .CH(c43), .CL(c03));
  FAGP fagp_2 (.ai(a6), .bi(b6), .ci(c6), .si(out_20), .gi(g6), .pi(p6));
  FAGP fagp_3 (.ai(a5), .bi(b5), .ci(c5), .si(out_21), .gi(g5), .pi(p5));
  BLOQUEB bloqueb_4 (.PH(p5), .PL(p4), .GH(g5), .GL(g4), .Cin(c42), .PHL(P5_4), .GHL(G5_4), .CH(c5), .CL(c4));
  FAGP fagp_4 (.ai(a4), .bi(b4), .ci(c4), .si(out_22), .gi(g4), .pi(p4));
  BLOQUEB bloqueb_5 (.PH(P3_2), .PL(P1_0), .GH(G3_2), .GL(G1_0), .Cin(c03), .PHL(P3_0), .GHL(G3_0), .CH(c22), .CL(c02));
  FAGP fagp_5 (.ai(a3), .bi(b3), .ci(c3), .si(out_23), .gi(g3), .pi(p3));
  BLOQUEB bloqueb_6 (.PH(p3), .PL(p2), .GH(g3), .GL(g2), .Cin(c22), .PHL(P3_2), .GHL(G3_2), .CH(c3), .CL(c2));
  FAGP fagp_6 (.ai(a2), .bi(b2), .ci(c2), .si(out_24), .gi(g2), .pi(p2));
  FAGP fagp_7 (.ai(a1), .bi(b1), .ci(c1), .si(out_25), .gi(g1), .pi(p1));
  BLOQUEB bloqueb_7 (.PH(p1), .PL(p0), .GH(g1), .GL(g0), .Cin(c02), .PHL(P1_0), .GHL(G1_0), .CH(c1), .CL(c0_t));
  FAGP fagp_8 (.ai(a0), .bi(b0), .ci(c0_t), .si(out_26), .gi(g0), .pi(p0));

  // Other names for the same wires on the sheet: p7 = out_18; s0 = out_26; s1 = out_25; s2 = out_24; s3 = out_23;
  //   s4 = out_22; s5 = out_21; s6 = out_20; s7 = out_19
endmodule

module BLOQUEB (
  input  PH,
  input  PL,
  input  GH,
  input  GL,
  input  Cin,
  output PHL,
  output GHL,
  output CH,
  output CL
);

  wire and_1_out, and_2_out;

  and and_1 (and_1_out, PH, GL);
  and and_2 (and_2_out, PL, Cin);
  and and_3 (PHL, PH, PL);
  or or_1 (GHL, GH, and_1_out);
  or or_2 (CH, and_2_out, GL);

  assign CL = Cin;
endmodule

module FAGP (
  input  ai,
  input  bi,
  input  ci,
  output si,
  output gi,
  output pi
);

  wire and_2_out, and_3_out, and_4_out, and_5_out, not_1_out, not_2_out, not_3_out, not_4_out, or_3_out;

  and and_1 (gi, bi, ai);
  or or_1 (pi, bi, ai);
  and and_2 (and_2_out, or_3_out, not_2_out);
  not not_1 (not_1_out, bi);
  and and_3 (and_3_out, ai, not_1_out);
  not not_2 (not_2_out, ci);
  and and_4 (and_4_out, ci, not_4_out);
  or or_2 (si, and_2_out, and_4_out);
  not not_3 (not_3_out, ai);
  and and_5 (and_5_out, not_3_out, bi);
  or or_3 (or_3_out, and_3_out, and_5_out);
  not not_4 (not_4_out, or_3_out);
endmodule
